# Fritzing sketch MC-38SecondaryDiagram (saved by Fritzing 0.9.10b)
breadboards: 1

parts:
  Componente1 = Arduino Nano (Rev3.0)
  S1 = MC-38  # not connected
  Componente4 = Arduino Uno (Rev3)

nets:
  N1: Componente1.A5, Componente4.A5/SCL
  N2: Componente1.A4, Componente4.A4/SDA

notes:
  Primário
  Secundário

custom parts:
  MC-38: MC-38 Contact Sensor w/ Reed Switch
