# Fritzing sketch MQ-2SecondaryDiagram (saved by Fritzing 0.9.10b)
breadboards: 1

parts:
  Componente1 = Arduino Nano (Rev3.0)
  Componente2 = MQ-9 breakout
  Componente3 = Arduino Uno (Rev3)

nets:
  GND: Componente1.GND, Componente2.GND
  5V: Componente1.5V, Componente2.VCC
  N1: Componente1.A7, Componente2.AO
  N2: Componente1.A5, Componente3.A5/SCL
  N3: Componente1.A4, Componente3.A4/SDA

notes:
  Primário
  Secundário

custom parts:
  MQ-9 breakout: SKU: 101284
