# Fritzing sketch PIRSecondaryDiagram (saved by Fritzing 0.9.10b)
breadboards: 1

parts:
  Componente1 = Arduino Nano (Rev3.0)
  PIR3 = PIR sensor
  Componente4 = Arduino Uno (Rev3)

nets:
  GND: Componente1.GND, PIR3.GND
  N1: Componente1.D2, PIR3.SIG
  5V: Componente1.5V, PIR3.VDD
  N2: Componente1.A5, Componente4.A5/SCL
  N3: Componente1.A4, Componente4.A4/SDA

notes:
  Primário
  Secundário
