# Fritzing sketch PrimaryDiagram (saved by Fritzing 0.9.10b)
breadboards: 2

parts:
  Componente1 = Arduino Uno (Rev3)
  LCD2 = LCD screen
  LCM1602_IIC1 = LCM1602 IIC [part_number="LCM1602 IIC" chip_label="LCM1602 IIC" package="DIP (Dual Inline) [THT]"]
  R1 = Resistor [tolerance=±5% resistance=10k package="0805 [SMD]"]
  R2 = Resistor [tolerance=±5% resistance=10k package="0805 [SMD]"]
  Keypad4x1 = Keypad Membran 4x4
  Componente4 = Arduino Nano (Rev3.0)
  Componente5 = Arduino Nano (Rev3.0)
  Componente6 = Arduino Nano (Rev3.0)
  R3 = Resistor [tolerance=±5% resistance=100 package="2512 [SMD]"]
  J1 = Piezo Speaker

nets:
  N1: Componente1.A4/SDA, LCM1602_IIC1.SDA, R2.Pin_0, Componente4.A4, Componente5.A4, Componente6.A4
  N2: Componente1.A5/SCL, LCM1602_IIC1.SCL, R1.Pin_0, Componente4.A5, Componente5.A5, Componente6.A5
  N3: Componente1.D8, Keypad4x1.Pin6
  N4: Componente1.D9_PWM, Keypad4x1.Pin7
  N5: Componente1.D10_PWM/SS, Keypad4x1.Pin8
  N6: Componente1.D3_PWM, Keypad4x1.Pin1
  N7: Componente1.D4, Keypad4x1.Pin2
  N8: Componente1.D5_PWM, Keypad4x1.Pin3
  N9: Componente1.D6_PWM, Keypad4x1.Pin4
  N10: Componente1.D7, Keypad4x1.Pin5
  5V: Componente1.5V, LCM1602_IIC1.VCC, R1.Pin_1, R2.Pin_1, R3.Pin_1
  GND: Componente1.GND, LCM1602_IIC1.GND, J1.pin1
  VSS: LCD2.VSS, LCM1602_IIC1.VSS
  VDD: LCD2.VDD, LCM1602_IIC1.VDD
  N11: LCD2.V0, LCM1602_IIC1.V0
  N12: LCD2.RS, LCM1602_IIC1.RS
  N13: LCD2.R/W, LCM1602_IIC1.RW
  N14: LCD2.E, LCM1602_IIC1.E
  N15: LCD2.DB0, LCM1602_IIC1.D0
  N16: LCD2.DB1, LCM1602_IIC1.D1
  N17: LCD2.DB2, LCM1602_IIC1.D2
  N18: LCD2.DB3, LCM1602_IIC1.D3
  N19: LCD2.DB4, LCM1602_IIC1.D4
  N20: LCD2.DB5, LCM1602_IIC1.D5
  N21: LCD2.DB6, LCM1602_IIC1.D6
  N22: LCD2.DB7, LCM1602_IIC1.D7
  N23: LCD2.LED+, LCM1602_IIC1.A
  N24: LCD2.LED-, LCM1602_IIC1.K
  N25: LCM1602_IIC1.LED_A, LCM1602_IIC1.LED_B
  N26: R3.Pin_0, J1.pin2

notes:
  I2C Bus
  Resistores Pull Up 10kΩ
  Secundário com o sensor PIR
  Secundário com o sensor MQ2
  Secundário com o sensor MC-38
  Primário
  Resistor de 100Ω

custom parts:
  LCM1602 IIC: I2C-Module to use a 1602 or 2004 LCD on with the wire.h libory Serial LCD Modul
  Keypad Membran 4x4: Membrane Keypad 4x4 Matrix
